// Logisim project dl shivani.8.circ as structural Verilog: 1 circuit, main circuit main
// CARRY
module main (
  input  in_1,
  input  in_2,
  input  in_3,
  output sum,
  output Carry
);

  wire and_1_out, and_2_out, xor_1_out;

  xor xor_1 (xor_1_out, in_1, in_2);
  xor xor_2 (sum, xor_1_out, in_3);
  and and_1 (and_1_out, xor_1_out, in_3);
  and and_2 (and_2_out, in_1, in_2);
  or or_1 (Carry, and_1_out, and_2_out);
endmodule
